// Logisim project segundero0-60.circ as structural Verilog: 6 circuits, main circuit hex0-9
module hex0_9 (
  input  sw5,
  input  sw4,
  input  sw3,
  input  sw2,
  input  sw1,
  input  sw0,
  output hex0,
  output hex1,
  output hex2,
  output hex3,
  output hex4,
  output hex5,
  output hex6,
  output hex7
);

  wire and_1_out, and_2_out, and_3_out, and_4_out, and_5_out, and_6_out, and_7_out, and_8_out, and_9_out,
       and_10_out, and_11_out, and_12_out, and_13_out, and_14_out, and_15_out, and_16_out, and_17_out,
       and_18_out, and_19_out, and_20_out, and_21_out, and_22_out, and_23_out, and_24_out, and_25_out,
       and_26_out, and_27_out, and_28_out, and_29_out, and_30_out, and_31_out, and_32_out, and_33_out,
       and_34_out, and_35_out, and_36_out, and_37_out, and_38_out, and_39_out, and_40_out, and_41_out,
       and_42_out, and_43_out, and_44_out, and_45_out, and_46_out, and_47_out, and_48_out, and_49_out,
       and_50_out, and_51_out, and_52_out, and_53_out, and_54_out, and_55_out, and_56_out, and_57_out,
       and_58_out, and_59_out, and_60_out, and_61_out, and_62_out, and_63_out, and_64_out, and_65_out,
       and_66_out, and_67_out, and_68_out, and_69_out, and_70_out, and_71_out, and_72_out, and_73_out,
       and_74_out, and_75_out, and_76_out, and_77_out, and_78_out, and_79_out, and_80_out, and_81_out,
       and_82_out, and_83_out, and_84_out, and_85_out, and_86_out, and_87_out, and_88_out, and_89_out,
       and_90_out, and_91_out, and_92_out, and_93_out, and_94_out, and_95_out, and_96_out, and_97_out,
       and_98_out, and_99_out, and_100_out, and_101_out, and_102_out, and_103_out, and_104_out, not_1_out,
       not_2_out, not_3_out, not_4_out, not_5_out, not_6_out, not_7_out, not_8_out, not_9_out, not_10_out,
       not_11_out, not_12_out, not_13_out, not_14_out, not_15_out, not_16_out, not_17_out, not_18_out,
       not_19_out, not_20_out, not_21_out, not_22_out, not_23_out, not_24_out, not_25_out, not_26_out,
       not_27_out, not_28_out, not_29_out, not_30_out, not_31_out, not_32_out, not_33_out, not_34_out,
       not_35_out, not_36_out, not_37_out, not_38_out, not_39_out, not_40_out, not_41_out, not_42_out,
       not_43_out, not_44_out, not_45_out, not_46_out, not_47_out, not_48_out, not_49_out, not_50_out,
       not_51_out, not_52_out, not_53_out, not_54_out, not_55_out, not_56_out, not_57_out, not_58_out,
       not_59_out, not_60_out, not_61_out, not_62_out, not_63_out, not_64_out, not_65_out, not_66_out,
       not_67_out, not_68_out, not_69_out, not_70_out, not_71_out, not_72_out, not_73_out, not_74_out,
       not_75_out, not_76_out, not_77_out, not_78_out, not_79_out, not_80_out, not_81_out, not_82_out,
       not_83_out, not_84_out, not_85_out, not_86_out, not_87_out, not_88_out, not_89_out, not_90_out,
       not_91_out, not_92_out, not_93_out, not_94_out, not_95_out, not_96_out, not_97_out, not_98_out,
       not_99_out, not_100_out, not_101_out, not_102_out, not_103_out, not_104_out, not_105_out, not_106_out,
       not_107_out, not_108_out, not_109_out, not_110_out, not_111_out, not_112_out, not_113_out,
       not_114_out, not_115_out, not_116_out, not_117_out, not_118_out, not_119_out, not_120_out,
       not_121_out, not_122_out, not_123_out, not_124_out, not_125_out, not_126_out, not_127_out,
       not_128_out, not_129_out, not_130_out, not_131_out, not_132_out, not_133_out, not_134_out,
       not_135_out, not_136_out, not_137_out, not_138_out, not_139_out, not_140_out, not_141_out,
       not_142_out, not_143_out, not_144_out, not_145_out, not_146_out, not_147_out, not_148_out,
       not_149_out, not_150_out, not_151_out, not_152_out, not_153_out, not_154_out, not_155_out,
       not_156_out, not_157_out, not_158_out, not_159_out, not_160_out, not_161_out, not_162_out,
       not_163_out, not_164_out, not_165_out, not_166_out, not_167_out, not_168_out, not_169_out,
       not_170_out, not_171_out, not_172_out, not_173_out, not_174_out, not_175_out, not_176_out,
       not_177_out, not_178_out, not_179_out, not_180_out, not_181_out, not_182_out, not_183_out,
       not_184_out, not_185_out, not_186_out, not_187_out, not_188_out, not_189_out, not_190_out,
       not_191_out, not_192_out, not_193_out, not_194_out, not_195_out, not_196_out, not_197_out,
       not_198_out, not_199_out, not_200_out, not_201_out, not_202_out, not_203_out, not_204_out,
       not_205_out, not_206_out, not_207_out, not_208_out, not_209_out, not_210_out, not_211_out,
       not_212_out, not_213_out, not_214_out, not_215_out, not_216_out, not_217_out, not_218_out,
       not_219_out, not_220_out, not_221_out, not_222_out, not_223_out, not_224_out, not_225_out,
       not_226_out, not_227_out, not_228_out, not_229_out;

  not not_1 (not_1_out, sw5);
  not not_2 (not_2_out, sw4);
  not not_3 (not_3_out, sw2);
  not not_4 (not_4_out, sw0);
  not not_5 (not_5_out, sw5);
  not not_6 (not_6_out, sw3);
  not not_7 (not_7_out, sw4);
  not not_8 (not_8_out, sw5);
  not not_9 (not_9_out, sw4);
  not not_10 (not_10_out, sw1);
  not not_11 (not_11_out, sw5);
  not not_12 (not_12_out, sw1);
  not not_13 (not_13_out, sw5);
  not not_14 (not_14_out, sw3);
  not not_15 (not_15_out, sw0);
  not not_16 (not_16_out, sw3);
  not not_17 (not_17_out, sw2);
  not not_18 (not_18_out, sw0);
  not not_19 (not_19_out, sw5);
  not not_20 (not_20_out, sw2);
  not not_21 (not_21_out, sw5);
  not not_22 (not_22_out, sw0);
  not not_23 (not_23_out, sw3);
  not not_24 (not_24_out, sw1);
  not not_25 (not_25_out, sw2);
  not not_26 (not_26_out, sw1);
  not not_27 (not_27_out, sw0);
  not not_28 (not_28_out, sw4);
  not not_29 (not_29_out, sw3);
  not not_30 (not_30_out, sw4);
  not not_31 (not_31_out, sw3);
  not not_32 (not_32_out, sw3);
  not not_33 (not_33_out, sw2);
  not not_34 (not_34_out, sw1);
  not not_35 (not_35_out, sw1);
  not not_36 (not_36_out, sw0);
  not not_37 (not_37_out, sw5);
  not not_38 (not_38_out, sw4);
  not not_39 (not_39_out, sw2);
  not not_40 (not_40_out, sw5);
  not not_41 (not_41_out, sw4);
  not not_42 (not_42_out, sw1);
  not not_43 (not_43_out, sw0);
  not not_44 (not_44_out, sw4);
  not not_45 (not_45_out, sw2);
  not not_46 (not_46_out, sw1);
  not not_47 (not_47_out, sw5);
  not not_48 (not_48_out, sw3);
  not not_49 (not_49_out, sw2);
  not not_50 (not_50_out, sw5);
  not not_51 (not_51_out, sw3);
  not not_52 (not_52_out, sw2);
  not not_53 (not_53_out, sw5);
  not not_54 (not_54_out, sw3);
  not not_55 (not_55_out, sw5);
  not not_56 (not_56_out, sw2);
  not not_57 (not_57_out, sw5);
  not not_58 (not_58_out, sw4);
  not not_59 (not_59_out, sw1);
  not not_60 (not_60_out, sw5);
  not not_61 (not_61_out, sw4);
  not not_62 (not_62_out, sw0);
  not not_63 (not_63_out, sw5);
  not not_64 (not_64_out, sw1);
  not not_65 (not_65_out, sw0);
  not not_66 (not_66_out, sw4);
  not not_67 (not_67_out, sw1);
  not not_68 (not_68_out, sw0);
  not not_69 (not_69_out, sw5);
  not not_70 (not_70_out, sw1);
  not not_71 (not_71_out, sw2);
  not not_72 (not_72_out, sw1);
  not not_73 (not_73_out, sw3);
  not not_74 (not_74_out, sw0);
  not not_75 (not_75_out, sw4);
  not not_76 (not_76_out, sw3);
  not not_77 (not_77_out, sw2);
  not not_78 (not_78_out, sw3);
  not not_79 (not_79_out, sw2);
  not not_80 (not_80_out, sw5);
  not not_81 (not_81_out, sw3);
  not not_82 (not_82_out, sw1);
  not not_83 (not_83_out, sw5);
  not not_84 (not_84_out, sw2);
  not not_85 (not_85_out, sw1);
  not not_86 (not_86_out, sw4);
  not not_87 (not_87_out, sw3);
  not not_88 (not_88_out, sw5);
  not not_89 (not_89_out, sw5);
  not not_90 (not_90_out, sw1);
  not not_91 (not_91_out, sw2);
  not not_92 (not_92_out, sw3);
  not not_93 (not_93_out, sw4);
  not not_94 (not_94_out, sw1);
  not not_95 (not_95_out, sw5);
  not not_96 (not_96_out, sw4);
  not not_97 (not_97_out, sw2);
  not not_98 (not_98_out, sw0);
  not not_99 (not_99_out, sw5);
  not not_100 (not_100_out, sw4);
  not not_101 (not_101_out, sw3);
  not not_102 (not_102_out, sw2);
  not not_103 (not_103_out, sw5);
  not not_104 (not_104_out, sw4);
  not not_105 (not_105_out, sw1);
  not not_106 (not_106_out, sw4);
  not not_107 (not_107_out, sw3);
  not not_108 (not_108_out, sw0);
  not not_109 (not_109_out, sw5);
  not not_110 (not_110_out, sw4);
  not not_111 (not_111_out, sw1);
  not not_112 (not_112_out, sw0);
  not not_113 (not_113_out, sw5);
  not not_114 (not_114_out, sw4);
  not not_115 (not_115_out, sw4);
  not not_116 (not_116_out, sw1);
  not not_117 (not_117_out, sw5);
  not not_118 (not_118_out, sw3);
  not not_119 (not_119_out, sw0);
  not not_120 (not_120_out, sw2);
  not not_121 (not_121_out, sw0);
  not not_122 (not_122_out, sw5);
  not not_123 (not_123_out, sw3);
  not not_124 (not_124_out, sw5);
  not not_125 (not_125_out, sw2);
  not not_126 (not_126_out, sw1);
  not not_127 (not_127_out, sw0);
  not not_128 (not_128_out, sw3);
  not not_129 (not_129_out, sw1);
  not not_130 (not_130_out, sw0);
  not not_131 (not_131_out, sw4);
  not not_132 (not_132_out, sw3);
  not not_133 (not_133_out, sw2);
  not not_134 (not_134_out, sw2);
  not not_135 (not_135_out, sw0);
  not not_136 (not_136_out, sw4);
  not not_137 (not_137_out, sw2);
  not not_138 (not_138_out, sw0);
  not not_139 (not_139_out, sw3);
  not not_140 (not_140_out, sw5);
  not not_141 (not_141_out, sw4);
  not not_142 (not_142_out, sw2);
  not not_143 (not_143_out, sw0);
  not not_144 (not_144_out, sw4);
  not not_145 (not_145_out, sw3);
  not not_146 (not_146_out, sw0);
  not not_147 (not_147_out, sw5);
  not not_148 (not_148_out, sw4);
  not not_149 (not_149_out, sw1);
  not not_150 (not_150_out, sw0);
  not not_151 (not_151_out, sw5);
  not not_152 (not_152_out, sw3);
  not not_153 (not_153_out, sw0);
  not not_154 (not_154_out, sw2);
  not not_155 (not_155_out, sw0);
  not not_156 (not_156_out, sw0);
  not not_157 (not_157_out, sw3);
  not not_158 (not_158_out, sw1);
  not not_159 (not_159_out, sw0);
  not not_160 (not_160_out, sw2);
  not not_161 (not_161_out, sw0);
  not not_162 (not_162_out, sw0);
  not not_163 (not_163_out, sw5);
  not not_164 (not_164_out, sw3);
  not not_165 (not_165_out, sw1);
  not not_166 (not_166_out, sw0);
  not not_167 (not_167_out, sw5);
  not not_168 (not_168_out, sw4);
  not not_169 (not_169_out, sw3);
  not not_170 (not_170_out, sw1);
  not not_171 (not_171_out, sw4);
  not not_172 (not_172_out, sw3);
  not not_173 (not_173_out, sw0);
  not not_174 (not_174_out, sw5);
  not not_175 (not_175_out, sw2);
  not not_176 (not_176_out, sw1);
  not not_177 (not_177_out, sw5);
  not not_178 (not_178_out, sw0);
  not not_179 (not_179_out, sw5);
  not not_180 (not_180_out, sw4);
  not not_181 (not_181_out, sw2);
  not not_182 (not_182_out, sw0);
  not not_183 (not_183_out, sw5);
  not not_184 (not_184_out, sw3);
  not not_185 (not_185_out, sw2);
  not not_186 (not_186_out, sw5);
  not not_187 (not_187_out, sw1);
  not not_188 (not_188_out, sw4);
  not not_189 (not_189_out, sw3);
  not not_190 (not_190_out, sw4);
  not not_191 (not_191_out, sw0);
  not not_192 (not_192_out, sw3);
  not not_193 (not_193_out, sw1);
  not not_194 (not_194_out, sw0);
  not not_195 (not_195_out, sw4);
  not not_196 (not_196_out, sw1);
  not not_197 (not_197_out, sw3);
  not not_198 (not_198_out, sw2);
  not not_199 (not_199_out, sw1);
  not not_200 (not_200_out, sw2);
  not not_201 (not_201_out, sw5);
  not not_202 (not_202_out, sw3);
  not not_203 (not_203_out, sw2);
  not not_204 (not_204_out, sw5);
  not not_205 (not_205_out, sw4);
  not not_206 (not_206_out, sw1);
  not not_207 (not_207_out, sw4);
  not not_208 (not_208_out, sw0);
  not not_209 (not_209_out, sw5);
  not not_210 (not_210_out, sw1);
  not not_211 (not_211_out, sw5);
  not not_212 (not_212_out, sw4);
  not not_213 (not_213_out, sw4);
  not not_214 (not_214_out, sw1);
  not not_215 (not_215_out, sw5);
  not not_216 (not_216_out, sw2);
  not not_217 (not_217_out, sw0);
  not not_218 (not_218_out, sw2);
  not not_219 (not_219_out, sw1);
  not not_220 (not_220_out, sw0);
  not not_221 (not_221_out, sw3);
  not not_222 (not_222_out, sw4);
  not not_223 (not_223_out, sw3);
  not not_224 (not_224_out, sw2);
  not not_225 (not_225_out, sw4);
  not not_226 (not_226_out, sw3);
  not not_227 (not_227_out, sw2);
  not not_228 (not_228_out, sw3);
  not not_229 (not_229_out, sw1);
  and and_1 (and_1_out, not_1_out, not_2_out, not_3_out, not_4_out);
  and and_2 (and_2_out, not_5_out, not_6_out, sw1);
  and and_3 (and_3_out, not_7_out, sw2, sw0);
  and and_4 (and_4_out, not_8_out, not_9_out, sw3, not_10_out);
  and and_5 (and_5_out, not_11_out, sw3, sw2, not_12_out);
  and and_6 (and_6_out, not_13_out, sw4, not_14_out, not_15_out);
  and and_7 (and_7_out, sw4, not_16_out, not_17_out, not_18_out);
  and and_8 (and_8_out, not_19_out, sw4, not_20_out, sw0);
  and and_9 (and_9_out, not_21_out, sw4, sw1, not_22_out);
  and and_10 (and_10_out, sw5, not_23_out, not_24_out);
  and and_11 (and_11_out, sw5, not_25_out, not_26_out, not_27_out);
  and and_12 (and_12_out, sw5, not_28_out, not_29_out, sw0);
  and and_13 (and_13_out, sw5, not_30_out, not_31_out, sw2);
  and and_14 (and_14_out, sw5, not_32_out, sw2, sw0);
  and and_15 (and_15_out, sw5, sw3, sw1);
  and and_16 (and_16_out, sw5, sw4, not_33_out, not_34_out);
  and and_17 (and_17_out, sw5, sw4, not_35_out, not_36_out);
  and and_18 (and_18_out, not_37_out, not_38_out, not_39_out);
  and and_19 (and_19_out, not_40_out, not_41_out, not_42_out, not_43_out);
  and and_20 (and_20_out, not_44_out, not_45_out, not_46_out);
  and and_21 (and_21_out, not_47_out, not_48_out, not_49_out, sw0);
  and and_22 (and_22_out, not_50_out, not_51_out, not_52_out, sw1);
  and and_23 (and_23_out, not_53_out, not_54_out, sw1, sw0);
  and and_24 (and_24_out, not_55_out, not_56_out, sw1, sw0);
  and and_25 (and_25_out, not_57_out, not_58_out, sw3, not_59_out);
  and and_26 (and_26_out, not_60_out, not_61_out, sw3, not_62_out);
  and and_27 (and_27_out, not_63_out, sw3, not_64_out, not_65_out);
  and and_28 (and_28_out, not_66_out, sw3, not_67_out, not_68_out);
  and and_29 (and_29_out, not_69_out, sw4, sw2);
  and and_30 (and_30_out, sw4, sw2, not_70_out);
  and and_31 (and_31_out, sw4, sw3, sw2);
  and and_32 (and_32_out, sw5, not_71_out, not_72_out, sw0);
  and and_33 (and_33_out, sw5, not_73_out, sw1, not_74_out);
  and and_34 (and_34_out, sw5, not_75_out, not_76_out, sw2, sw0);
  and and_35 (and_35_out, sw5, sw3, not_77_out, sw1);
  and and_36 (and_36_out, sw5, sw3, sw1, sw0);
  and and_37 (and_37_out, sw5, sw4, not_78_out, not_79_out);
  and and_38 (and_38_out, not_80_out, not_81_out, not_82_out);
  and and_39 (and_39_out, not_83_out, not_84_out, not_85_out);
  and and_40 (and_40_out, not_86_out, not_87_out, sw2);
  and and_41 (and_41_out, not_88_out, sw3, sw1);
  and and_42 (and_42_out, not_89_out, sw4, not_90_out);
  and and_43 (and_43_out, sw4, not_91_out);
  and and_44 (and_44_out, sw5, not_92_out, sw1);
  and and_45 (and_45_out, sw5, not_93_out, sw2);
  and and_46 (and_46_out, sw5, sw3, not_94_out);
  and and_47 (and_47_out, not_95_out, not_96_out, not_97_out, not_98_out);
  and and_48 (and_48_out, not_99_out, not_100_out, not_101_out, not_102_out, sw1);
  and and_49 (and_49_out, not_103_out, not_104_out, sw2, not_105_out, sw0);
  and and_50 (and_50_out, not_106_out, not_107_out, sw2, sw1, not_108_out);
  and and_51 (and_51_out, not_109_out, not_110_out, sw3, not_111_out, not_112_out);
  and and_52 (and_52_out, not_113_out, not_114_out, sw3, sw2, sw0);
  and and_53 (and_53_out, not_115_out, sw3, sw2, not_116_out, sw0);
  and and_54 (and_54_out, not_117_out, sw4, not_118_out, not_119_out);
  and and_55 (and_55_out, sw4, not_120_out, sw1, not_121_out);
  and and_56 (and_56_out, not_122_out, sw4, not_123_out, sw2, sw1);
  and and_57 (and_57_out, not_124_out, sw4, sw3, not_125_out, not_126_out, sw0);
  and and_58 (and_58_out, sw4, sw3, sw2, not_127_out);
  and and_59 (and_59_out, sw5, not_128_out, not_129_out, not_130_out);
  and and_60 (and_60_out, sw5, not_131_out, not_132_out, not_133_out, sw0);
  and and_61 (and_61_out, sw5, sw3, not_134_out, not_135_out);
  and and_62 (and_62_out, sw5, not_136_out, sw3, not_137_out, sw1);
  and and_63 (and_63_out, sw5, sw3, sw1, not_138_out);
  and and_64 (and_64_out, sw5, sw4, not_139_out, sw2, sw0);
  and and_65 (and_65_out, sw5, sw4, sw3, sw2, sw1);
  and and_66 (and_66_out, not_140_out, not_141_out, not_142_out, not_143_out);
  and and_67 (and_67_out, not_144_out, not_145_out, sw2, sw1, not_146_out);
  and and_68 (and_68_out, not_147_out, not_148_out, sw3, not_149_out, not_150_out);
  and and_69 (and_69_out, not_151_out, sw4, not_152_out, not_153_out);
  and and_70 (and_70_out, sw4, not_154_out, sw1, not_155_out);
  and and_71 (and_71_out, sw4, sw3, sw2, not_156_out);
  and and_72 (and_72_out, sw5, not_157_out, not_158_out, not_159_out);
  and and_73 (and_73_out, sw5, sw3, not_160_out, not_161_out);
  and and_74 (and_74_out, sw5, sw3, sw1, not_162_out);
  and and_75 (and_75_out, not_163_out, not_164_out, not_165_out, not_166_out);
  and and_76 (and_76_out, not_167_out, not_168_out, not_169_out, sw2, not_170_out);
  and and_77 (and_77_out, not_171_out, not_172_out, sw2, not_173_out);
  and and_78 (and_78_out, not_174_out, sw3, not_175_out, not_176_out);
  and and_79 (and_79_out, not_177_out, sw3, sw1, not_178_out);
  and and_80 (and_80_out, not_179_out, not_180_out, sw3, sw2, sw1);
  and and_81 (and_81_out, sw4, not_181_out, not_182_out);
  and and_82 (and_82_out, not_183_out, sw4, not_184_out, not_185_out, sw1);
  and and_83 (and_83_out, not_186_out, sw4, sw3, not_187_out);
  and and_84 (and_84_out, sw5, not_188_out, not_189_out, sw1);
  and and_85 (and_85_out, sw5, not_190_out, sw2, not_191_out);
  and and_86 (and_86_out, sw5, not_192_out, sw2, sw1);
  and and_87 (and_87_out, sw5, sw3, not_193_out, not_194_out);
  and and_88 (and_88_out, sw5, not_195_out, sw3, sw2, not_196_out);
  and and_89 (and_89_out, sw5, sw4, not_197_out, not_198_out, not_199_out);
  and and_90 (and_90_out, sw5, sw4, sw3, not_200_out, sw1);
  and and_91 (and_91_out, not_201_out, not_202_out, not_203_out, sw1);
  and and_92 (and_92_out, not_204_out, not_205_out, sw2, not_206_out);
  and and_93 (and_93_out, not_207_out, sw2, not_208_out);
  and and_94 (and_94_out, not_209_out, sw3, not_210_out);
  and and_95 (and_95_out, not_211_out, not_212_out, sw3, sw2);
  and and_96 (and_96_out, not_213_out, sw3, sw2, not_214_out);
  and and_97 (and_97_out, not_215_out, sw4, not_216_out, not_217_out);
  and and_98 (and_98_out, sw4, not_218_out, not_219_out, not_220_out);
  and and_99 (and_99_out, sw4, not_221_out, sw2, sw1);
  and and_100 (and_100_out, sw5, not_222_out, not_223_out, not_224_out);
  and and_101 (and_101_out, sw5, not_225_out, not_226_out, sw1);
  and and_102 (and_102_out, sw5, sw3, not_227_out, sw1);
  and and_103 (and_103_out, sw5, sw4, not_228_out, not_229_out);
  and and_104 (and_104_out, sw5, sw4, sw3, sw1);
  or or_1 (hex2, and_38_out, and_39_out, sw0, and_40_out, and_41_out, and_42_out, and_43_out, and_44_out, and_45_out, and_46_out);
  or or_2 (hex4, and_66_out, and_67_out, and_68_out, and_69_out, and_70_out, and_71_out, and_72_out, and_73_out, and_74_out);
  or or_3 (hex0, and_1_out, and_2_out, and_3_out, and_4_out, and_5_out, and_6_out, and_7_out, and_8_out, and_9_out, and_10_out, and_11_out, and_12_out, and_13_out, and_14_out, and_15_out, and_16_out, and_17_out);
  or or_4 (hex1, and_18_out, and_19_out, and_20_out, and_21_out, and_22_out, and_23_out, and_24_out, and_25_out, and_26_out, and_27_out, and_28_out, and_29_out, and_30_out, and_31_out, and_32_out, and_33_out, and_34_out, and_35_out, and_36_out, and_37_out);
  or or_5 (hex3, and_47_out, and_48_out, and_49_out, and_50_out, and_51_out, and_52_out, and_53_out, and_54_out, and_55_out, and_56_out, and_57_out, and_58_out, and_59_out, and_60_out, and_61_out, and_62_out, and_63_out, and_64_out, and_65_out);
  or or_6 (hex5, and_75_out, and_76_out, and_77_out, and_78_out, and_79_out, and_80_out, and_81_out, and_82_out, and_83_out, and_84_out, and_85_out, and_86_out, and_87_out, and_88_out, and_89_out, and_90_out);
  or or_7 (hex6, and_91_out, and_92_out, and_93_out, and_94_out, and_95_out, and_96_out, and_97_out, and_98_out, and_99_out, and_100_out, and_101_out, and_102_out, and_103_out, and_104_out);

  assign hex7 = 1'b0;
endmodule

module DECODERBCD (
  input  [3:0] in_1
);

  wire compa_1_out, hex0, hex1, hex2, hex3, hex4, hex5, hex6, hex7, hex8, hex9, hex10, hex11, hex12, hex13;
  wire [3:0] bin_bin_1_o3, multiplexer_1_out;

  Multiplexer #(.width(4), .enable("false")) multiplexer_1 (
    .in0(in_1), .in1(bin_bin_1_o3), .out(multiplexer_1_out), .sel(compa_1_out));
  compa compa_1 (.i3(in_1[3]), .i2(in_1[2]), .i1(in_1[1]), .i0(in_1[0]), .out(compa_1_out));
  BIN_BIN bin_bin_1 (
    .B3(in_1[3]), .B2(in_1[2]), .B1(in_1[1]), .B0(in_1[0]), .O3(bin_bin_1_o3[0]), .O2(bin_bin_1_o3[1]),
    .O1(bin_bin_1_o3[2]), .O0(bin_bin_1_o3[3]));
  hex0_9 _0_1 (
    .sw4(1'b0), .sw3(1'b0), .sw2(1'b0), .sw1(compa_1_out), .hex0(hex0), .hex1(hex1), .hex2(hex2),
    .hex3(hex3), .hex4(hex4), .hex5(hex5), .hex6(hex6));  // open: sw5, sw0, hex7
  hex0_9 _0_9 (
    .sw4(multiplexer_1_out[0]), .sw3(multiplexer_1_out[1]), .sw2(multiplexer_1_out[2]),
    .sw1(multiplexer_1_out[3]), .hex0(hex7), .hex1(hex8), .hex2(hex9), .hex3(hex10), .hex4(hex11),
    .hex5(hex12), .hex6(hex13));  // open: sw5, sw0, hex7
  _7_Segment_Display u_7_segment_display_1 (
    .g(hex6), .f(hex5), .a(hex0), .b(hex1), .e(hex4), .d(hex3), .c(hex2));  // open: dp
  _7_Segment_Display u_7_segment_display_2 (
    .g(hex13), .f(hex12), .a(hex7), .b(hex8), .e(hex11), .d(hex10), .c(hex9));  // open: dp
endmodule

module BIN_BIN (
  input  B3,
  input  B2,
  input  B1,
  input  B0,
  output O3,
  output O2,
  output O1,
  output O0
);

  wire and_1_out, and_2_out, and_3_out, and_4_out, and_5_out, not_1_out, not_2_out, not_3_out, not_4_out,
       not_5_out, not_6_out, not_7_out;

  not not_1 (not_1_out, B3);
  and and_1 (and_1_out, not_1_out, not_2_out, B0);
  not not_2 (not_2_out, B1);
  not not_3 (not_3_out, B2);
  and and_2 (and_2_out, not_3_out, not_4_out, B0);
  not not_4 (not_4_out, B1);
  and and_3 (and_3_out, B2, B1);
  not not_5 (not_5_out, B1);
  and and_4 (and_4_out, not_5_out, not_6_out);
  not not_6 (not_6_out, B0);
  and and_5 (and_5_out, B3, B2, not_7_out);
  not not_7 (not_7_out, B1);
  or or_1 (O2, and_1_out, and_2_out, and_3_out);
  or or_2 (O1, and_4_out, and_5_out);

  assign O0 = B0;
  assign O3 = 1'b0;
endmodule

module compa (
  input  i3,
  input  i2,
  input  i1,
  input  i0,
  output out
);

  wire and_1_out, and_2_out;

  and and_1 (and_1_out, i3, i1);
  and and_2 (and_2_out, i3, i2);
  or or_1 (out, and_1_out, and_2_out);
endmodule

module dec0_1 (
);

  wire clock_1_out, comparator_1_eq, comparator_2_eq, hex0, hex1, hex2, hex3, hex4, hex5, hex6, hex7, hex10,
       hex11, hex12, hex13, hex14, hex15, hex16, hex17, multiplexer_1_out, multiplexer_2_out, Reset_out;
  wire [5:0] adder_1_out, adder_2_out, register_1_q, register_2_q;

  Clock clock_1 (.out(clock_1_out));
  Button Reset (.out(Reset_out));
  Register #(.width(6)) register_1 (
    .D(adder_1_out), .Q(register_1_q), .clk(clock_1_out), .clr(multiplexer_1_out));  // open: en
  Adder #(.width(6)) adder_1 (.a(register_1_q), .b(6'b000001), .out(adder_1_out));  // open: cin, cout
  Multiplexer #(.enable("false")) multiplexer_1 (
    .in0(comparator_1_eq), .in1(Reset_out), .out(multiplexer_1_out), .sel(Reset_out));
  Comparator #(.width(6)) comparator_1 (.a(register_1_q), .b(6'b100000), .eq(comparator_1_eq));  // open: gt, lt
  Adder #(.width(6)) adder_2 (.a(register_2_q), .b(6'b000001), .out(adder_2_out));  // open: cin, cout
  Register #(.width(6)) register_2 (
    .D(adder_2_out), .Q(register_2_q), .clk(comparator_1_eq), .clr(multiplexer_2_out));  // open: en
  Multiplexer #(.enable("false")) multiplexer_2 (
    .in0(comparator_2_eq), .in1(Reset_out), .out(multiplexer_2_out), .sel(Reset_out));
  hex0_9 hex0_9_1 (
    .sw5(register_2_q[5]), .sw4(register_2_q[4]), .sw3(register_2_q[3]), .sw2(register_2_q[2]),
    .sw1(register_2_q[1]), .sw0(register_2_q[0]), .hex0(hex0), .hex1(hex1), .hex2(hex2), .hex3(hex3),
    .hex4(hex4), .hex5(hex5), .hex6(hex6), .hex7(hex7));
  hex1 hex1_1 (
    .sw5(register_2_q[5]), .sw4(register_2_q[4]), .sw3(register_2_q[3]), .sw2(register_2_q[2]),
    .sw1(register_2_q[1]), .sw0(register_2_q[0]), .hex10(hex10), .hex11(hex11), .hex12(hex12), .hex13(hex13),
    .hex14(hex14), .hex15(hex15), .hex16(hex16), .hex17(hex17));
  Comparator #(.width(6)) comparator_2 (.a(register_2_q), .b(6'b111100), .eq(comparator_2_eq));  // open: gt, lt
  _7_Segment_Display u_7_segment_display_1 (
    .g(hex16), .f(hex15), .a(hex10), .b(hex11), .e(hex14), .d(hex13), .c(hex12), .dp(hex17));
  _7_Segment_Display u_7_segment_display_2 (
    .g(hex6), .f(hex5), .a(hex0), .b(hex1), .e(hex4), .d(hex3), .c(hex2), .dp(hex7));
endmodule

module hex1 (
  input  sw5,
  input  sw4,
  input  sw3,
  input  sw2,
  input  sw1,
  input  sw0,
  output hex10,
  output hex11,
  output hex12,
  output hex13,
  output hex14,
  output hex15,
  output hex16,
  output hex17
);

  wire and_1_out, and_2_out, and_3_out, and_4_out, and_5_out, and_6_out, and_7_out, and_8_out, and_9_out,
       and_10_out, and_11_out, and_12_out, and_13_out, and_14_out, and_15_out, and_16_out, and_17_out,
       and_18_out, and_19_out, and_20_out, and_21_out, and_22_out, and_23_out, and_24_out, and_25_out,
       not_1_out, not_2_out, not_3_out, not_4_out, not_5_out, not_6_out, not_7_out, not_8_out, not_9_out,
       not_10_out, not_11_out, not_12_out, not_13_out, not_14_out, not_15_out, not_16_out, not_17_out,
       not_18_out, not_19_out, not_20_out, not_21_out, not_22_out, not_23_out, not_24_out, not_25_out,
       not_26_out, not_27_out, not_28_out, not_29_out, not_30_out, not_31_out, not_32_out, not_33_out,
       not_34_out, not_35_out, not_36_out, not_37_out, not_38_out, not_39_out, not_40_out, not_41_out,
       not_42_out, not_43_out, not_44_out;

  not not_1 (not_1_out, sw5);
  not not_2 (not_2_out, sw4);
  not not_3 (not_3_out, sw2);
  not not_4 (not_4_out, sw1);
  not not_5 (not_5_out, sw4);
  not not_6 (not_6_out, sw3);
  not not_7 (not_7_out, sw3);
  not not_8 (not_8_out, sw3);
  not not_9 (not_9_out, sw3);
  not not_10 (not_10_out, sw2);
  not not_11 (not_11_out, sw1);
  not not_12 (not_12_out, sw3);
  not not_13 (not_13_out, sw2);
  not not_14 (not_14_out, sw5);
  not not_15 (not_15_out, sw4);
  not not_16 (not_16_out, sw2);
  not not_17 (not_17_out, sw1);
  not not_18 (not_18_out, sw4);
  not not_19 (not_19_out, sw3);
  not not_20 (not_20_out, sw3);
  not not_21 (not_21_out, sw3);
  not not_22 (not_22_out, sw5);
  not not_23 (not_23_out, sw4);
  not not_24 (not_24_out, sw3);
  not not_25 (not_25_out, sw5);
  not not_26 (not_26_out, sw4);
  not not_27 (not_27_out, sw2);
  not not_28 (not_28_out, sw1);
  not not_29 (not_29_out, sw5);
  not not_30 (not_30_out, sw3);
  not not_31 (not_31_out, sw5);
  not not_32 (not_32_out, sw2);
  not not_33 (not_33_out, sw5);
  not not_34 (not_34_out, sw1);
  not not_35 (not_35_out, sw5);
  not not_36 (not_36_out, sw4);
  not not_37 (not_37_out, sw3);
  not not_38 (not_38_out, sw5);
  not not_39 (not_39_out, sw4);
  not not_40 (not_40_out, sw2);
  not not_41 (not_41_out, sw1);
  and and_1 (and_1_out, sw4, sw2);
  and and_2 (and_2_out, sw4, sw3);
  and and_3 (and_3_out, not_1_out, not_2_out, not_3_out, not_4_out);
  and and_4 (and_4_out, not_5_out, not_6_out);
  and and_5 (and_5_out, not_7_out, sw2);
  and and_6 (and_6_out, sw4, sw3);
  and and_7 (and_7_out, sw5, not_8_out, sw1);
  not not_42 (not_42_out, sw5);
  not not_43 (not_43_out, sw4);
  and and_8 (and_8_out, not_9_out, not_10_out, not_11_out);
  not not_44 (not_44_out, sw4);
  and and_9 (and_9_out, not_12_out, not_13_out);
  and and_10 (and_10_out, sw3, sw2, sw1);
  and and_11 (and_11_out, not_14_out, not_15_out, not_16_out, not_17_out);
  and and_12 (and_12_out, not_18_out, not_19_out);
  and and_13 (and_13_out, not_20_out, sw2);
  and and_14 (and_14_out, sw4, sw3);
  and and_15 (and_15_out, sw5, not_21_out, sw1);
  and and_16 (and_16_out, not_22_out, not_23_out, not_24_out);
  and and_17 (and_17_out, not_25_out, not_26_out, not_27_out, not_28_out);
  and and_18 (and_18_out, not_29_out, not_30_out, sw2);
  and and_19 (and_19_out, not_31_out, sw4, sw3, not_32_out);
  and and_20 (and_20_out, not_33_out, sw4, sw3, not_34_out);
  and and_21 (and_21_out, sw5, sw4, sw3, sw2);
  and and_22 (and_22_out, not_35_out, not_36_out, not_37_out);
  and and_23 (and_23_out, not_38_out, not_39_out, not_40_out, not_41_out);
  and and_24 (and_24_out, sw5, sw3);
  and and_25 (and_25_out, sw5, sw4);
  or or_1 (hex16, and_1_out, and_2_out, sw5);
  or or_2 (hex10, and_3_out, and_4_out, and_5_out, and_6_out, and_7_out);
  or or_3 (hex11, not_42_out, not_43_out, and_8_out);
  or or_4 (hex12, not_44_out, and_9_out, and_10_out, sw5);
  or or_5 (hex13, and_11_out, and_12_out, and_13_out, and_14_out, and_15_out);
  or or_6 (hex14, and_16_out, and_17_out, and_18_out, and_19_out, and_20_out, and_21_out);
  or or_7 (hex15, and_22_out, and_23_out, and_24_out, and_25_out);

  assign hex17 = 1'b0;
endmodule
