// Logisim project booths.circ as structural Verilog: 3 circuits, main circuit datapath
module datapath (
  input  [7:0] Q,
  input  [7:0] M,
  input  mux1,
  input  load,
  input  Shift_Enable,
  input  clear,
  input  clk,
  output [16:0] Shift_Out,
  output negative,
  output DONE
);

  wire not_2_out, not_3_out, xor_1_out;
  wire [4:0] adder_1_out, register_1_q;
  wire [7:0] adder_2_out, adder_3_out, multiplexer_3_out, not_1_out;
  wire [15:0] adder_4_out, multiplexer_4_out, not_4_out;
  wire [15:1] undriven;
  wire [16:0] multiplexer_1_out, multiplexer_2_out;
  wire [16:9] shift_register_1_q7;

  Multiplexer #(.width(17), .enable("false")) multiplexer_1 (
    .in0(multiplexer_2_out), .in1({{8{1'b0}}, Q, 1'b0}), .out(multiplexer_1_out), .sel(mux1));
  xor xor_1 (xor_1_out, multiplexer_2_out[0], multiplexer_2_out[1]);
  assign not_1_out = ~M;  // NOT_Gate not_1, 8 bits wide
  Register #(.width(5)) register_1 (.D(adder_1_out), .en(not_2_out), .Q(register_1_q), .clk(clk));  // open: clr
  Adder #(.width(5)) adder_1 (.a(register_1_q), .b(5'b00001), .out(adder_1_out));  // open: cin, cout
  not not_2 (not_2_out, DONE);
  Adder adder_2 (.a(not_1_out), .b(8'h1), .out(adder_2_out));  // open: cin, cout
  Multiplexer #(.width(8), .enable("false")) multiplexer_2 (
    .in0(shift_register_1_q7), .in1(adder_3_out), .out(multiplexer_2_out[16:9]), .sel(xor_1_out));
  Shift_Register #(.length(17)) shift_register_1 (
    .shift(Shift_Enable), .in(multiplexer_1_out[16]), .clk(clk), .load(load), .clr(clear),
    .d0(multiplexer_1_out[16]), .q0(shift_register_1_q7[16]), .d1(multiplexer_1_out[15]),
    .q1(shift_register_1_q7[15]), .d2(multiplexer_1_out[14]), .q2(shift_register_1_q7[14]),
    .d3(multiplexer_1_out[13]), .q3(shift_register_1_q7[13]), .d4(multiplexer_1_out[12]),
    .q4(shift_register_1_q7[12]), .d5(multiplexer_1_out[11]), .q5(shift_register_1_q7[11]),
    .d6(multiplexer_1_out[10]), .q6(shift_register_1_q7[10]), .d7(multiplexer_1_out[9]),
    .q7(shift_register_1_q7[9]), .d8(multiplexer_1_out[8]), .q8(multiplexer_2_out[8]),
    .d9(multiplexer_1_out[7]), .q9(multiplexer_2_out[7]), .d10(multiplexer_1_out[6]),
    .q10(multiplexer_2_out[6]), .d11(multiplexer_1_out[5]), .q11(multiplexer_2_out[5]),
    .d12(multiplexer_1_out[4]), .q12(multiplexer_2_out[4]), .d13(multiplexer_1_out[3]),
    .q13(multiplexer_2_out[3]), .d14(multiplexer_1_out[2]), .q14(multiplexer_2_out[2]),
    .d15(multiplexer_1_out[1]), .q15(multiplexer_2_out[1]), .d16(multiplexer_1_out[0]),
    .q16(multiplexer_2_out[0]));  // open: out
  Multiplexer #(.width(8), .enable("false")) multiplexer_3 (
    .in0(M), .in1(adder_2_out), .out(multiplexer_3_out), .sel(multiplexer_2_out[1]));
  Comparator #(.width(5)) comparator_1 (.a(register_1_q), .b(5'b10011), .eq(DONE));  // open: gt, lt
  Adder adder_3 (.a(multiplexer_3_out), .b(shift_register_1_q7), .out(adder_3_out));  // open: cin, cout
  not not_3 (not_3_out, DONE);
  Register #(.width(17)) register_2 (
    .D({shift_register_1_q7, multiplexer_2_out[8:0]}), .en(not_3_out), .Q(Shift_Out), .clk(clk));  // open: clr
  assign not_4_out = ~{negative, undriven};  // NOT_Gate not_4, 16 bits wide
  Adder #(.width(16)) adder_4 (.a(not_4_out), .b(16'h1), .out(adder_4_out));  // open: cin, cout
  Multiplexer #(.width(16), .enable("false")) multiplexer_4 (
    .in0({negative, undriven}), .in1(adder_4_out), .out(multiplexer_4_out), .sel(negative));
endmodule

module controller (
  input  go,
  input  S1,
  input  S0,
  output N1,
  output N0,
  output muxE,
  output load,
  output shift,
  output clear
);

  wire and_2_out, and_3_out, and_4_out, and_5_out, not_1_out, not_2_out;

  or or_1 (N1, S0, S1);
  not not_1 (not_1_out, S0);
  not not_2 (not_2_out, S1);
  and and_1 (shift, S1, S0);
  and and_2 (and_2_out, not_1_out, go);
  and and_3 (and_3_out, S1, not_1_out);
  and and_4 (and_4_out, not_2_out, S0);
  and and_5 (and_5_out, S1, not_1_out);
  and and_6 (clear, not_2_out, not_1_out, go);
  or or_2 (N0, and_2_out, and_3_out);
  and and_7 (muxE, not_2_out, S0);
  or or_3 (load, and_4_out, and_5_out);
endmodule

module main (
  input  go,
  input  [7:0] Q,
  input  [7:0] M,
  output [16:0] result,
  output negative,
  output done
);

  wire clock_1_out, controller_1_clear, controller_1_load, controller_1_muxe, controller_1_shift;
  wire [1:0] controller_1_n0, register_1_q;

  Register #(.width(2)) register_1 (.D(controller_1_n0), .Q(register_1_q), .clk(clock_1_out), .clr(done));  // open: en
  controller controller_1 (
    .go(go), .S1(register_1_q[1]), .S0(register_1_q[0]), .N1(controller_1_n0[1]), .N0(controller_1_n0[0]),
    .muxE(controller_1_muxe), .load(controller_1_load), .shift(controller_1_shift), .clear(controller_1_clear));
  Clock clock_1 (.out(clock_1_out));
  datapath datapath_1 (
    .mux1(controller_1_muxe), .load(controller_1_load), .Shift_Enable(controller_1_shift),
    .clear(controller_1_clear), .DONE(done), .Q(Q), .M(M), .clk(clock_1_out), .Shift_Out(result));  // open: negative
endmodule
