// Logisim project KeyboardCtrl.circ as structural Verilog: 2 circuits, main circuit main
module main (
  input  in_1,
  input  load,
  input  ShiftEn
);

  wire comparator_1_eq, H0, H0_1, H0_2, H0_3, H1, H1_1, H1_2, H1_3, H2, H2_1, H2_2, H2_3, H3, H3_1, H3_2,
       H3_3, H4, H4_1, H4_2, H4_3, H5, H5_1, H5_2, H5_3, H6, H6_1, H6_2, H6_3, not_1_out, not_2_out,
       ps2CLK_out;
  wire [3:0] adder_1_out, register_1_q;
  wire [7:0] shift_register_1_q8, shift_register_2_q0, shift_register_2_q1, shift_register_2_q2,
       shift_register_2_q3;

  Clock ps2CLK (.out(ps2CLK_out));
  _7_Segment_Display u_7_segment_display_1 (
    .g(H6_1), .f(H5_1), .a(H0_1), .b(H1_1), .e(H4_1), .d(H3_1), .c(H2_1));  // open: dp
  Shift_Register #(.length(11), .trigger("falling")) shift_register_1 (
    .shift(ShiftEn), .in(in_1), .clk(ps2CLK_out), .load(load), .q1(shift_register_1_q8[7]),
    .q2(shift_register_1_q8[6]), .q3(shift_register_1_q8[5]), .q4(shift_register_1_q8[4]),
    .q5(shift_register_1_q8[3]), .q6(shift_register_1_q8[2]), .q7(shift_register_1_q8[1]),
    .q8(shift_register_1_q8[0]));  // open: out, clr, d0, q0, d1, d2, d3, d4, d5, d6, d7, d8, d9, q9, d10, q10
  _7_Segment_Display u_7_segment_display_2 (.g(H6), .f(H5), .a(H0), .b(H1), .e(H4), .d(H3), .c(H2));  // open: dp
  Shift_Register #(.width(8), .length(4), .trigger("falling")) shift_register_2 (
    .shift(ShiftEn), .in(shift_register_1_q8), .clk(not_1_out), .q0(shift_register_2_q0),
    .q1(shift_register_2_q1), .q2(shift_register_2_q2), .q3(shift_register_2_q3));  // open: out, load, clr, d0, d1, d2, d3
  not not_1 (not_1_out, comparator_1_eq);
  Adder #(.width(4)) adder_1 (.a(register_1_q), .b(4'b0001), .out(adder_1_out));  // open: cin, cout
  not not_2 (not_2_out, ps2CLK_out);
  _7_Segment_Display u_7_segment_display_3 (
    .g(H6_2), .f(H5_2), .a(H0_2), .b(H1_2), .e(H4_2), .d(H3_2), .c(H2_2));  // open: dp
  Register #(.width(4), .trigger("falling")) register_1 (
    .D(adder_1_out), .Q(register_1_q), .clk(not_2_out), .clr(comparator_1_eq));  // open: en
  Comparator #(.width(4)) comparator_1 (.a(register_1_q), .b(4'b1100), .eq(comparator_1_eq));  // open: gt, lt
  _7_Segment_Display u_7_segment_display_4 (
    .g(H6_3), .f(H5_3), .a(H0_3), .b(H1_3), .e(H4_3), .d(H3_3), .c(H2_3));  // open: dp
  decoder decoder_1 (
    .S0(shift_register_2_q1[7]), .S1(shift_register_2_q1[6]), .S2(shift_register_2_q1[5]),
    .S3(shift_register_2_q1[4]), .S4(shift_register_2_q1[3]), .S5(shift_register_2_q1[2]),
    .S6(shift_register_2_q1[1]), .S7(shift_register_2_q1[0]), .H0(H0), .H1(H1), .H2(H2), .H3(H3), .H4(H4),
    .H5(H5), .H6(H6));
  decoder decoder_2 (
    .S0(shift_register_2_q3[7]), .S1(shift_register_2_q3[6]), .S2(shift_register_2_q3[5]),
    .S3(shift_register_2_q3[4]), .S4(shift_register_2_q3[3]), .S5(shift_register_2_q3[2]),
    .S6(shift_register_2_q3[1]), .S7(shift_register_2_q3[0]), .H0(H0_3), .H1(H1_3), .H2(H2_3), .H3(H3_3),
    .H4(H4_3), .H5(H5_3), .H6(H6_3));
  decoder decoder_3 (
    .S0(shift_register_2_q0[7]), .S1(shift_register_2_q0[6]), .S2(shift_register_2_q0[5]),
    .S3(shift_register_2_q0[4]), .S4(shift_register_2_q0[3]), .S5(shift_register_2_q0[2]),
    .S6(shift_register_2_q0[1]), .S7(shift_register_2_q0[0]), .H0(H0_1), .H1(H1_1), .H2(H2_1), .H3(H3_1),
    .H4(H4_1), .H5(H5_1), .H6(H6_1));
  decoder decoder_4 (
    .S0(shift_register_2_q2[7]), .S1(shift_register_2_q2[6]), .S2(shift_register_2_q2[5]),
    .S3(shift_register_2_q2[4]), .S4(shift_register_2_q2[3]), .S5(shift_register_2_q2[2]),
    .S6(shift_register_2_q2[1]), .S7(shift_register_2_q2[0]), .H0(H0_2), .H1(H1_2), .H2(H2_2), .H3(H3_2),
    .H4(H4_2), .H5(H5_2), .H6(H6_2));
endmodule

module decoder (
  input  S0,
  input  S1,
  input  S2,
  input  S3,
  input  S4,
  input  S5,
  input  S6,
  input  S7,
  output H0,
  output H1,
  output H2,
  output H3,
  output H4,
  output H5,
  output H6
);

  wire and_1_out, and_2_out, and_3_out, and_4_out, and_5_out, and_6_out, and_7_out, and_8_out, and_9_out,
       and_10_out, and_11_out, and_12_out, and_13_out, and_14_out, and_15_out, and_16_out, and_17_out,
       and_18_out, and_19_out, and_20_out, and_21_out, and_22_out, and_23_out, and_24_out, and_25_out,
       and_26_out, and_27_out, and_28_out, and_29_out, and_30_out, and_31_out, and_32_out, and_33_out,
       and_34_out, and_35_out, and_36_out, and_37_out, and_38_out, and_39_out, and_40_out, and_41_out,
       and_42_out, and_43_out, and_44_out, and_45_out, and_46_out, and_47_out, and_48_out, and_49_out,
       and_50_out, and_51_out, not_1_out, not_2_out, not_3_out, not_4_out, not_5_out, not_6_out, not_7_out,
       not_8_out, not_9_out, not_10_out, not_11_out, not_12_out, not_13_out, not_14_out, not_15_out,
       not_16_out, not_17_out, not_18_out, not_19_out, not_20_out, not_21_out, not_22_out, not_23_out,
       not_24_out, not_25_out, not_26_out, not_27_out, not_28_out, not_29_out, not_30_out, not_31_out,
       not_32_out, not_33_out, not_34_out, not_35_out, not_36_out, not_37_out, not_38_out, not_39_out,
       not_40_out, not_41_out, not_42_out, not_43_out, not_44_out, not_45_out, not_46_out, not_47_out,
       not_48_out, not_49_out, not_50_out, not_51_out, not_52_out, not_53_out, not_54_out, not_55_out,
       not_56_out, not_57_out, not_58_out, not_59_out, not_60_out, not_61_out, not_62_out, not_63_out,
       not_64_out, not_65_out, not_66_out, not_67_out, not_68_out, not_69_out, not_70_out, not_71_out,
       not_72_out, not_73_out;

  not not_1 (not_1_out, S2);
  not not_2 (not_2_out, S0);
  not not_3 (not_3_out, S4);
  not not_4 (not_4_out, S5);
  not not_5 (not_5_out, S6);
  not not_6 (not_6_out, S3);
  not not_7 (not_7_out, S4);
  not not_8 (not_8_out, S7);
  not not_9 (not_9_out, S2);
  and and_1 (and_1_out, not_9_out, S7);
  not not_10 (not_10_out, S2);
  and and_2 (and_2_out, not_10_out, S6);
  and and_3 (and_3_out, S5, not_11_out);
  not not_11 (not_11_out, S6);
  and and_4 (and_4_out, S3, not_12_out);
  not not_12 (not_12_out, S6);
  and and_5 (and_5_out, S2, not_13_out, not_14_out);
  not not_13 (not_13_out, S6);
  not not_14 (not_14_out, S7);
  and and_6 (and_6_out, S1, not_15_out);
  not not_15 (not_15_out, S6);
  and and_7 (and_7_out, S0, not_16_out);
  not not_16 (not_16_out, S6);
  not not_17 (not_17_out, S2);
  not not_18 (not_18_out, S4);
  not not_19 (not_19_out, S4);
  not not_20 (not_20_out, S4);
  not not_21 (not_21_out, S4);
  not not_22 (not_22_out, S0);
  not not_23 (not_23_out, S1);
  not not_24 (not_24_out, S6);
  not not_25 (not_25_out, S7);
  not not_26 (not_26_out, S7);
  not not_27 (not_27_out, S4);
  not not_28 (not_28_out, S4);
  not not_29 (not_29_out, S5);
  not not_30 (not_30_out, S7);
  not not_31 (not_31_out, S7);
  not not_32 (not_32_out, S0);
  not not_33 (not_33_out, S3);
  not not_34 (not_34_out, S4);
  not not_35 (not_35_out, S5);
  not not_36 (not_36_out, S6);
  not not_37 (not_37_out, S4);
  not not_38 (not_38_out, S7);
  not not_39 (not_39_out, S7);
  not not_40 (not_40_out, S7);
  not not_41 (not_41_out, S2);
  not not_42 (not_42_out, S0);
  not not_43 (not_43_out, S3);
  not not_44 (not_44_out, S4);
  not not_45 (not_45_out, S5);
  not not_46 (not_46_out, S6);
  not not_47 (not_47_out, S7);
  not not_48 (not_48_out, S6);
  not not_49 (not_49_out, S3);
  not not_50 (not_50_out, S3);
  not not_51 (not_51_out, S3);
  not not_52 (not_52_out, S3);
  not not_53 (not_53_out, S0);
  not not_54 (not_54_out, S1);
  not not_55 (not_55_out, S6);
  not not_56 (not_56_out, S7);
  not not_57 (not_57_out, S7);
  not not_58 (not_58_out, S3);
  not not_59 (not_59_out, S3);
  not not_60 (not_60_out, S1);
  not not_61 (not_61_out, S2);
  not not_62 (not_62_out, S3);
  not not_63 (not_63_out, S1);
  not not_64 (not_64_out, S3);
  not not_65 (not_65_out, S1);
  not not_66 (not_66_out, S3);
  not not_67 (not_67_out, S1);
  not not_68 (not_68_out, S3);
  not not_69 (not_69_out, S7);
  not not_70 (not_70_out, S7);
  not not_71 (not_71_out, S7);
  not not_72 (not_72_out, S1);
  not not_73 (not_73_out, S3);
  and and_8 (and_8_out, not_1_out, S4);
  and and_9 (and_9_out, S3, S4);
  and and_10 (and_10_out, not_2_out, S2, not_3_out, not_4_out, not_5_out);
  and and_11 (and_11_out, S2, not_6_out, not_7_out, not_8_out);
  and and_12 (and_12_out, S2, S3, S7);
  and and_13 (and_13_out, S2, S3, S5);
  and and_14 (and_14_out, S0, S2, S3);
  and and_15 (and_15_out, not_17_out, not_18_out, S7);
  and and_16 (and_16_out, not_19_out, S6);
  and and_17 (and_17_out, not_20_out, S5);
  and and_18 (and_18_out, S3, not_21_out);
  and and_19 (and_19_out, not_22_out, not_23_out, S3, S5, not_24_out, not_25_out);
  and and_20 (and_20_out, S2, not_26_out);
  and and_21 (and_21_out, S2, S4);
  and and_22 (and_22_out, S1, not_27_out);
  and and_23 (and_23_out, S0, not_28_out);
  and and_24 (and_24_out, S3, S4, not_29_out, not_30_out);
  and and_25 (and_25_out, S3, S4, S6, not_31_out);
  and and_26 (and_26_out, not_32_out, S2, not_33_out, not_34_out, not_35_out, not_36_out);
  and and_27 (and_27_out, S2, not_37_out, not_38_out);
  and and_28 (and_28_out, S2, S3, not_39_out);
  and and_29 (and_29_out, S1, S7);
  and and_30 (and_30_out, S1, S3, S4);
  and and_31 (and_31_out, S0, S3, S4, not_40_out);
  and and_32 (and_32_out, not_41_out, S4);
  and and_33 (and_33_out, not_42_out, S2, not_43_out, not_44_out, not_45_out, not_46_out, S7);
  and and_34 (and_34_out, S2, S3, not_47_out);
  and and_35 (and_35_out, S1, not_48_out);
  and and_36 (and_36_out, not_49_out, S7);
  and and_37 (and_37_out, not_50_out, S6);
  and and_38 (and_38_out, not_51_out, S5);
  and and_39 (and_39_out, not_52_out, S4);
  and and_40 (and_40_out, not_53_out, not_54_out, S4, S5, not_55_out, not_56_out);
  and and_41 (and_41_out, S2, not_57_out);
  and and_42 (and_42_out, S1, not_58_out);
  and and_43 (and_43_out, S0, not_59_out);
  and and_44 (and_44_out, not_60_out, not_61_out, not_62_out, S7);
  and and_45 (and_45_out, not_63_out, not_64_out, S6);
  and and_46 (and_46_out, not_65_out, not_66_out, S5);
  and and_47 (and_47_out, not_67_out, not_68_out, S4);
  and and_48 (and_48_out, S4, not_69_out);
  and and_49 (and_49_out, S2, not_70_out);
  and and_50 (and_50_out, S1, not_71_out);
  and and_51 (and_51_out, S0, not_72_out, not_73_out);
  or or_1 (H0, and_8_out, and_9_out, and_10_out, and_11_out, and_12_out, and_13_out, S1, and_14_out);
  or or_2 (H1, and_1_out, and_2_out, and_3_out, S4, and_4_out, and_5_out, and_6_out, and_7_out);
  or or_3 (H2, and_15_out, and_16_out, and_17_out, and_18_out, and_19_out, and_20_out, and_21_out, and_22_out, and_23_out);
  or or_4 (H3, and_24_out, and_25_out, and_26_out, and_27_out, and_28_out, and_29_out, and_30_out, and_31_out);
  or or_5 (H4, and_32_out, and_33_out, and_34_out, and_35_out);
  or or_6 (H5, and_36_out, and_37_out, and_38_out, and_39_out, and_40_out, and_41_out, and_42_out, and_43_out);
  or or_7 (H6, and_44_out, and_45_out, and_46_out, and_47_out, and_48_out, and_49_out, and_50_out, and_51_out);
endmodule
