// Logisim project Ps2.circ as structural Verilog: 5 circuits, main circuit keyboardEmulator
// KEYBOARD
module keyboardEmulator (
  input  [2:0] Selector,
  input  Ps2CLK,
  output Data,
  output clk
);

  wire comparator_1_eq, comparator_2_gt, comparator_3_eq, comparator_4_eq, comparator_5_eq, comparator_6_eq,
       not_1_out, not_2_out;
  wire [5:0] adder_1_out, adder_2_out, adder_3_out, register_1_q, register_2_q, register_3_q;
  wire [7:0] multiplexer_1_out, multiplexer_3_out;

  Multiplexer #(.select(3), .width(8), .enable("false")) multiplexer_1 (
    .in0(8'h1e), .in1(8'h36), .in2(8'h3d), .in3(8'h46), .in4(8'h1c), .in5(8'h32), .in6(8'h44), .in7(8'h29),
    .out(multiplexer_1_out), .sel(Selector));
  Multiplexer #(.enable("false")) multiplexer_2 (.in0(Ps2CLK), .out(clk), .sel(comparator_2_gt));  // open: in1
  Adder #(.width(6)) adder_1 (.a(register_2_q), .b(6'b000001), .out(adder_1_out));  // open: cin, cout
  not not_1 (not_1_out, Ps2CLK);
  Adder #(.width(6)) adder_2 (.a(register_3_q), .b(6'b000001), .out(adder_2_out));  // open: cin, cout
  Adder #(.width(6)) adder_3 (.a(register_1_q), .b(6'b000001), .out(adder_3_out));  // open: cin, cout
  Register #(.width(6), .trigger("falling")) register_1 (
    .D(adder_3_out), .Q(register_1_q), .clk(clk), .clr(comparator_1_eq));  // open: en
  Register #(.width(6)) register_2 (
    .D(adder_1_out), .Q(register_2_q), .clk(not_1_out), .clr(comparator_5_eq));  // open: en
  Multiplexer #(.width(8), .enable("false")) multiplexer_3 (
    .in0(multiplexer_1_out), .in1(8'hf0), .out(multiplexer_3_out), .sel(comparator_3_eq));
  Register #(.width(6), .trigger("falling")) register_3 (
    .D(adder_2_out), .Q(register_3_q), .clk(comparator_1_eq), .clr(comparator_4_eq));  // open: en
  Comparator #(.width(6), .mode("unsigned")) comparator_1 (
    .a(register_1_q), .b(6'b001011), .eq(comparator_1_eq));  // open: gt, lt
  Comparator #(.width(6)) comparator_2 (.a(register_2_q), .b(6'b001010), .gt(comparator_2_gt));  // open: eq, lt
  Comparator #(.width(6), .mode("unsigned")) comparator_3 (
    .a(register_3_q), .b(6'b000001), .eq(comparator_3_eq));  // open: gt, lt
  Comparator #(.width(6), .mode("unsigned")) comparator_4 (
    .a(register_3_q), .b(6'b000010), .eq(comparator_4_eq));  // open: gt, lt
  Comparator #(.width(6)) comparator_5 (.a(register_2_q), .b(6'b001101), .eq(comparator_5_eq));  // open: gt, lt
  not not_2 (not_2_out, comparator_6_eq);
  Shift_Register #(.length(11)) shift_register_1 (
    .shift(not_2_out), .in(1'b0), .clk(clk), .out(Data), .load(comparator_6_eq), .d0(1'b0),
    .d1(multiplexer_3_out[7]), .d2(multiplexer_3_out[6]), .d3(multiplexer_3_out[5]),
    .d4(multiplexer_3_out[4]), .d5(multiplexer_3_out[3]), .d6(multiplexer_3_out[2]),
    .d7(multiplexer_3_out[1]), .d8(multiplexer_3_out[0]), .d9(1'b0), .d10(1'b0));  // open: clr, q0, q1, q2, q3, q4, q5, q6, q7, q8, q9, q10
  Comparator #(.width(6)) comparator_6 (.a(register_1_q), .b({6{1'b0}}), .eq(comparator_6_eq));  // open: gt, lt
endmodule

module PS2CONTROL (
  input  [2:0] selector
);

  wire comparator_1_eq, comparator_2_eq, comparator_3_eq, fpgaclk_out, H0, H0_1, H0_2, H0_3, H1, H1_1, H1_2,
       H1_3, H2, H2_1, H2_2, H2_3, H3, H3_1, H3_2, H3_3, H4, H4_1, H4_2, H4_3, H5, H5_1, H5_2, H5_3, H6,
       H6_1, H6_2, H6_3, keyboardemulator_1_clk, keyboardemulator_1_data, not_1_out, not_2_out, register_1_q,
       register_3_q, synch_1_midout;
  wire [5:0] counter_1_count, synch_1_count;
  wire [7:0] register_2_q, register_4_q, shift_register_1_q8, shift_register_2_q0, shift_register_2_q1,
       shift_register_2_q2, shift_register_2_q3;

  Clock ps2clk ();  // open: out
  Clock fpgaclk (.out(fpgaclk_out));
  _7_Segment_Display u_7_segment_display_1 (
    .g(H6_3), .f(H5_3), .a(H0_3), .b(H1_3), .e(H4_3), .d(H3_3), .c(H2_3));  // open: dp
  keyboardEmulator keyboardemulator_1 (
    .Selector(selector), .Ps2CLK(fpgaclk_out), .Data(keyboardemulator_1_data), .clk(keyboardemulator_1_clk));
  counter counter_1 (.clk(keyboardemulator_1_clk), .count(counter_1_count), .clear(register_3_q));
  Shift_Register #(.length(11)) shift_register_1 (
    .in(keyboardemulator_1_data), .clk(not_1_out), .q1(shift_register_1_q8[7]), .q2(shift_register_1_q8[6]),
    .q3(shift_register_1_q8[5]), .q4(shift_register_1_q8[4]), .q5(shift_register_1_q8[3]),
    .q6(shift_register_1_q8[2]), .q7(shift_register_1_q8[1]), .q8(shift_register_1_q8[0]));  // open: shift, out, load, clr, d0, q0, d1, d2, d3, d4, d5, d6, d7, d8, d9, q9, d10, q10
  not not_1 (not_1_out, keyboardemulator_1_clk);
  Comparator #(.width(6)) comparator_1 (.a(6'b001010), .b(counter_1_count), .eq(comparator_1_eq));  // open: gt, lt
  Register #(.width(1)) register_1 (.D(comparator_1_eq), .Q(register_1_q), .clk(fpgaclk_out));  // open: en, clr
  _7_Segment_Display u_7_segment_display_2 (
    .g(H6_2), .f(H5_2), .a(H0_2), .b(H1_2), .e(H4_2), .d(H3_2), .c(H2_2));  // open: dp
  Register register_2 (
    .D(shift_register_1_q8), .en(register_1_q), .Q(register_2_q), .clk(fpgaclk_out), .clr(comparator_3_eq));
  Register #(.width(1)) register_3 (.D(register_1_q), .Q(register_3_q), .clk(fpgaclk_out));  // open: en, clr
  Synch synch_1 (
    .PS2CLK(keyboardemulator_1_clk), .FPGACLK(fpgaclk_out), .MIDOUT(synch_1_midout), .COUNT(synch_1_count));
  Comparator comparator_2 (.a(register_2_q), .b(8'hf0), .eq(comparator_2_eq));  // open: gt, lt
  _7_Segment_Display u_7_segment_display_3 (.g(H6), .f(H5), .a(H0), .b(H1), .e(H4), .d(H3), .c(H2));  // open: dp
  Register register_4 (.D(register_2_q), .en(not_2_out), .Q(register_4_q), .clk(fpgaclk_out), .clr(comparator_3_eq));
  not not_2 (not_2_out, comparator_2_eq);
  Comparator #(.width(6)) comparator_3 (.a(synch_1_count), .b(6'b100001), .eq(comparator_3_eq));  // open: gt, lt
  _7_Segment_Display u_7_segment_display_4 (
    .g(H6_1), .f(H5_1), .a(H0_1), .b(H1_1), .e(H4_1), .d(H3_1), .c(H2_1));  // open: dp
  Shift_Register #(.width(8), .length(4), .trigger("falling")) shift_register_2 (
    .shift(synch_1_midout), .in(register_4_q), .clk(fpgaclk_out), .q0(shift_register_2_q0),
    .q1(shift_register_2_q1), .q2(shift_register_2_q2), .q3(shift_register_2_q3));  // open: out, load, clr, d0, d1, d2, d3
  DECODER decoder_1 (
    .S0(shift_register_2_q0[7]), .S1(shift_register_2_q0[6]), .S2(shift_register_2_q0[5]),
    .S3(shift_register_2_q0[4]), .S4(shift_register_2_q0[3]), .S5(shift_register_2_q0[2]),
    .S6(shift_register_2_q0[1]), .S7(shift_register_2_q0[0]), .H0(H0_1), .H1(H1_1), .H2(H2_1), .H3(H3_1),
    .H4(H4_1), .H5(H5_1), .H6(H6_1));
  DECODER decoder_2 (
    .S0(shift_register_2_q3[7]), .S1(shift_register_2_q3[6]), .S2(shift_register_2_q3[5]),
    .S3(shift_register_2_q3[4]), .S4(shift_register_2_q3[3]), .S5(shift_register_2_q3[2]),
    .S6(shift_register_2_q3[1]), .S7(shift_register_2_q3[0]), .H0(H0_3), .H1(H1_3), .H2(H2_3), .H3(H3_3),
    .H4(H4_3), .H5(H5_3), .H6(H6_3));
  DECODER decoder_3 (
    .S0(shift_register_2_q1[7]), .S1(shift_register_2_q1[6]), .S2(shift_register_2_q1[5]),
    .S3(shift_register_2_q1[4]), .S4(shift_register_2_q1[3]), .S5(shift_register_2_q1[2]),
    .S6(shift_register_2_q1[1]), .S7(shift_register_2_q1[0]), .H0(H0), .H1(H1), .H2(H2), .H3(H3), .H4(H4),
    .H5(H5), .H6(H6));
  DECODER decoder_4 (
    .S0(shift_register_2_q2[7]), .S1(shift_register_2_q2[6]), .S2(shift_register_2_q2[5]),
    .S3(shift_register_2_q2[4]), .S4(shift_register_2_q2[3]), .S5(shift_register_2_q2[2]),
    .S6(shift_register_2_q2[1]), .S7(shift_register_2_q2[0]), .H0(H0_2), .H1(H1_2), .H2(H2_2), .H3(H3_2),
    .H4(H4_2), .H5(H5_2), .H6(H6_2));
endmodule

// SYSCOUNT
module counter (
  input  clear,
  input  clk,
  output [5:0] count
);

  wire not_1_out;
  wire [5:0] adder_1_out;

  Adder #(.width(6)) adder_1 (.a(count), .b(6'b000001), .out(adder_1_out));  // open: cin, cout
  not not_1 (not_1_out, clk);
  Register #(.width(6)) register_1 (.D(adder_1_out), .Q(count), .clk(not_1_out), .clr(clear));  // open: en
endmodule

module Synch (
  input  FPGACLK,
  input  PS2CLK,
  output MIDOUT,
  output [5:0] COUNT
);

  wire comparator_1_eq, register_2_q;

  counter counter_1 (.clk(PS2CLK), .count(COUNT), .clear(register_2_q));
  Comparator #(.width(6)) comparator_1 (.a(COUNT), .b(6'b100000), .eq(comparator_1_eq));  // open: gt, lt
  Register #(.width(1)) register_1 (.D(comparator_1_eq), .Q(MIDOUT), .clk(FPGACLK));  // open: en, clr
  Register #(.width(1)) register_2 (.D(MIDOUT), .Q(register_2_q), .clk(FPGACLK));  // open: en, clr
endmodule

module DECODER (
  input  S0,
  input  S1,
  input  S2,
  input  S3,
  input  S4,
  input  S5,
  input  S6,
  input  S7,
  output H0,
  output H1,
  output H2,
  output H3,
  output H4,
  output H5,
  output H6
);

  wire and_1_out, and_2_out, and_3_out, and_4_out, and_5_out, and_6_out, and_7_out, and_8_out, and_9_out,
       and_10_out, and_11_out, and_12_out, and_13_out, and_14_out, and_15_out, and_16_out, and_17_out,
       and_18_out, and_19_out, and_20_out, and_21_out, and_22_out, and_23_out, and_24_out, and_25_out,
       and_26_out, and_27_out, and_28_out, and_29_out, and_30_out, and_31_out, and_32_out, and_33_out,
       and_34_out, and_35_out, and_36_out, and_37_out, and_38_out, and_39_out, and_40_out, and_41_out,
       and_42_out, and_43_out, and_44_out, and_45_out, and_46_out, and_47_out, and_48_out, and_49_out,
       and_50_out, and_51_out, and_52_out, and_53_out, and_54_out, and_55_out, and_56_out, and_57_out,
       and_58_out, and_59_out, and_60_out, and_61_out, and_62_out, and_63_out, and_64_out, not_1_out,
       not_2_out, not_3_out, not_4_out, not_5_out, not_6_out, not_7_out, not_8_out, not_9_out, not_10_out,
       not_11_out, not_12_out, not_13_out, not_14_out, not_15_out, not_16_out, not_17_out, not_18_out,
       not_19_out, not_20_out, not_21_out, not_22_out, not_23_out, not_24_out, not_25_out, not_26_out,
       not_27_out, not_28_out, not_29_out, not_30_out, not_31_out, not_32_out, not_33_out, not_34_out,
       not_35_out, not_36_out, not_37_out, not_38_out, not_39_out, not_40_out, not_41_out, not_42_out,
       not_43_out, not_44_out, not_45_out, not_46_out, not_47_out, not_48_out, not_49_out, not_50_out,
       not_51_out, not_52_out, not_53_out, not_54_out, not_55_out, not_56_out, not_57_out, not_58_out,
       not_59_out, not_60_out, not_61_out, not_62_out, not_63_out, not_64_out, not_65_out, not_66_out,
       not_67_out, not_68_out, not_69_out, not_70_out, not_71_out, not_72_out, not_73_out, not_74_out,
       not_75_out, not_76_out, not_77_out, not_78_out, not_79_out, not_80_out, not_81_out, not_82_out,
       not_83_out, not_84_out, not_85_out, not_86_out, not_87_out, not_88_out, not_89_out, not_90_out,
       not_91_out, not_92_out, not_93_out, not_94_out, not_95_out, not_96_out, not_97_out, not_98_out,
       not_99_out, not_100_out, not_101_out, not_102_out, not_103_out, not_104_out, not_105_out;

  not not_1 (not_1_out, S2);
  not not_2 (not_2_out, S0);
  not not_3 (not_3_out, S6);
  not not_4 (not_4_out, S0);
  not not_5 (not_5_out, S4);
  not not_6 (not_6_out, S5);
  not not_7 (not_7_out, S6);
  not not_8 (not_8_out, S3);
  not not_9 (not_9_out, S4);
  not not_10 (not_10_out, S7);
  not not_11 (not_11_out, S2);
  not not_12 (not_12_out, S2);
  not not_13 (not_13_out, S4);
  not not_14 (not_14_out, S6);
  not not_15 (not_15_out, S7);
  not not_16 (not_16_out, S6);
  not not_17 (not_17_out, S0);
  not not_18 (not_18_out, S1);
  not not_19 (not_19_out, S5);
  not not_20 (not_20_out, S6);
  not not_21 (not_21_out, S7);
  not not_22 (not_22_out, S6);
  not not_23 (not_23_out, S6);
  not not_24 (not_24_out, S2);
  not not_25 (not_25_out, S4);
  not not_26 (not_26_out, S4);
  not not_27 (not_27_out, S4);
  not not_28 (not_28_out, S4);
  not not_29 (not_29_out, S0);
  not not_30 (not_30_out, S1);
  not not_31 (not_31_out, S6);
  not not_32 (not_32_out, S7);
  not not_33 (not_33_out, S7);
  not not_34 (not_34_out, S4);
  not not_35 (not_35_out, S4);
  not not_36 (not_36_out, S5);
  not not_37 (not_37_out, S7);
  not not_38 (not_38_out, S7);
  not not_39 (not_39_out, S0);
  not not_40 (not_40_out, S3);
  not not_41 (not_41_out, S4);
  not not_42 (not_42_out, S5);
  not not_43 (not_43_out, S6);
  not not_44 (not_44_out, S4);
  not not_45 (not_45_out, S7);
  not not_46 (not_46_out, S7);
  not not_47 (not_47_out, S0);
  not not_48 (not_48_out, S3);
  not not_49 (not_49_out, S4);
  not not_50 (not_50_out, S6);
  not not_51 (not_51_out, S7);
  not not_52 (not_52_out, S2);
  not not_53 (not_53_out, S0);
  not not_54 (not_54_out, S3);
  not not_55 (not_55_out, S6);
  not not_56 (not_56_out, S0);
  not not_57 (not_57_out, S3);
  not not_58 (not_58_out, S4);
  not not_59 (not_59_out, S5);
  not not_60 (not_60_out, S6);
  not not_61 (not_61_out, S7);
  not not_62 (not_62_out, S0);
  not not_63 (not_63_out, S1);
  not not_64 (not_64_out, S4);
  not not_65 (not_65_out, S5);
  not not_66 (not_66_out, S6);
  not not_67 (not_67_out, S3);
  not not_68 (not_68_out, S4);
  not not_69 (not_69_out, S3);
  not not_70 (not_70_out, S3);
  not not_71 (not_71_out, S2);
  not not_72 (not_72_out, S3);
  not not_73 (not_73_out, S0);
  not not_74 (not_74_out, S1);
  not not_75 (not_75_out, S6);
  not not_76 (not_76_out, S7);
  not not_77 (not_77_out, S7);
  not not_78 (not_78_out, S0);
  not not_79 (not_79_out, S1);
  not not_80 (not_80_out, S4);
  not not_81 (not_81_out, S5);
  not not_82 (not_82_out, S3);
  not not_83 (not_83_out, S3);
  not not_84 (not_84_out, S1);
  not not_85 (not_85_out, S2);
  not not_86 (not_86_out, S3);
  not not_87 (not_87_out, S1);
  not not_88 (not_88_out, S3);
  not not_89 (not_89_out, S1);
  not not_90 (not_90_out, S3);
  not not_91 (not_91_out, S4);
  not not_92 (not_92_out, S7);
  not not_93 (not_93_out, S7);
  not not_94 (not_94_out, S0);
  not not_95 (not_95_out, S1);
  not not_96 (not_96_out, S4);
  not not_97 (not_97_out, S5);
  not not_98 (not_98_out, S5);
  not not_99 (not_99_out, S7);
  not not_100 (not_100_out, S7);
  not not_101 (not_101_out, S7);
  not not_102 (not_102_out, S1);
  not not_103 (not_103_out, S3);
  not not_104 (not_104_out, S3);
  not not_105 (not_105_out, S7);
  and and_1 (and_1_out, not_1_out, S4);
  and and_2 (and_2_out, not_2_out, S4, S5, not_3_out, S7);
  and and_3 (and_3_out, S3, S4);
  and and_4 (and_4_out, not_4_out, S2, not_5_out, not_6_out, not_7_out);
  and and_5 (and_5_out, S2, not_8_out, not_9_out, not_10_out);
  and and_6 (and_6_out, S2, S3, S5);
  and and_7 (and_7_out, S0, S2, S3);
  and and_8 (and_8_out, not_11_out, S7);
  and and_9 (and_9_out, not_12_out, S6);
  and and_10 (and_10_out, not_13_out, S5, not_14_out);
  and and_11 (and_11_out, S4, not_15_out);
  and and_12 (and_12_out, S4, S6);
  and and_13 (and_13_out, S3, not_16_out);
  and and_14 (and_14_out, not_17_out, not_18_out, S3, not_19_out, S7);
  and and_15 (and_15_out, S2, not_20_out, not_21_out);
  and and_16 (and_16_out, S1, not_22_out);
  and and_17 (and_17_out, S0, not_23_out);
  and and_18 (and_18_out, not_24_out, not_25_out, S7);
  and and_19 (and_19_out, not_26_out, S6);
  and and_20 (and_20_out, not_27_out, S5);
  and and_21 (and_21_out, S3, not_28_out);
  and and_22 (and_22_out, not_29_out, not_30_out, S3, S5, not_31_out, not_32_out);
  and and_23 (and_23_out, S2, not_33_out);
  and and_24 (and_24_out, S2, S6);
  and and_25 (and_25_out, S2, S3);
  and and_26 (and_26_out, S1, not_34_out);
  and and_27 (and_27_out, S1, S2);
  and and_28 (and_28_out, S0, not_35_out);
  and and_29 (and_29_out, S0, S2);
  and and_30 (and_30_out, S3, S4, not_36_out, not_37_out);
  and and_31 (and_31_out, S3, S4, S6, not_38_out);
  and and_32 (and_32_out, not_39_out, S2, not_40_out, not_41_out, not_42_out, not_43_out);
  and and_33 (and_33_out, S2, not_44_out, not_45_out);
  and and_34 (and_34_out, S2, S3, not_46_out);
  and and_35 (and_35_out, S1, S7);
  and and_36 (and_36_out, not_47_out, S1, not_48_out, not_49_out, S5, not_50_out);
  and and_37 (and_37_out, S1, S3, S4);
  and and_38 (and_38_out, S0, S3, S4, not_51_out);
  and and_39 (and_39_out, not_52_out, S4);
  and and_40 (and_40_out, not_53_out, not_54_out, S4, S5, not_55_out, S7);
  and and_41 (and_41_out, not_56_out, S2, not_57_out, not_58_out, not_59_out, not_60_out, S7);
  and and_42 (and_42_out, S2, S3, not_61_out);
  and and_43 (and_43_out, not_62_out, not_63_out, S2, S3, not_64_out, not_65_out, S6);
  and and_44 (and_44_out, S1, not_66_out);
  and and_45 (and_45_out, not_67_out, not_68_out, S7);
  and and_46 (and_46_out, not_69_out, S6);
  and and_47 (and_47_out, not_70_out, S5);
  and and_48 (and_48_out, not_71_out, not_72_out, S4);
  and and_49 (and_49_out, not_73_out, not_74_out, S4, S5, not_75_out, not_76_out);
  and and_50 (and_50_out, S2, not_77_out);
  and and_51 (and_51_out, not_78_out, not_79_out, S2, not_80_out, not_81_out, S6);
  and and_52 (and_52_out, S1, not_82_out);
  and and_53 (and_53_out, S0, not_83_out);
  and and_54 (and_54_out, not_84_out, not_85_out, not_86_out, S7);
  and and_55 (and_55_out, not_87_out, not_88_out, S6);
  and and_56 (and_56_out, not_89_out, not_90_out, not_91_out, S5);
  and and_57 (and_57_out, S4, not_92_out);
  and and_58 (and_58_out, S2, not_93_out);
  and and_59 (and_59_out, not_94_out, not_95_out, S2, not_96_out, not_97_out, S6);
  and and_60 (and_60_out, S1, not_98_out, not_99_out);
  and and_61 (and_61_out, S1, S6, not_100_out);
  and and_62 (and_62_out, S1, S3, not_101_out);
  and and_63 (and_63_out, S0, not_102_out, not_103_out);
  and and_64 (and_64_out, S0, not_104_out, not_105_out);
  or or_1 (H0, and_1_out, and_2_out, and_3_out, and_4_out, and_5_out, and_6_out, S1, and_7_out);
  or or_2 (H1, and_8_out, and_9_out, and_10_out, and_11_out, and_12_out, and_13_out, and_14_out, and_15_out, and_16_out, and_17_out);
  or or_3 (H2, and_18_out, and_19_out, and_20_out, and_21_out, and_22_out, and_23_out, and_24_out, and_25_out, and_26_out, and_27_out, and_28_out, and_29_out);
  or or_4 (H3, and_30_out, and_31_out, and_32_out, and_33_out, and_34_out, and_35_out, and_36_out, and_37_out, and_38_out);
  or or_5 (H4, and_39_out, and_40_out, and_41_out, and_42_out, and_43_out, and_44_out);
  or or_6 (H5, and_45_out, and_46_out, and_47_out, and_48_out, and_49_out, and_50_out, and_51_out, and_52_out, and_53_out);
  or or_7 (H6, and_54_out, and_55_out, and_56_out, and_57_out, and_58_out, and_59_out, and_60_out, and_61_out, and_62_out, and_63_out, and_64_out);
endmodule
